// Logisim project circuit.circ as structural Verilog: 3 circuits, main circuit main
module main (
  input  in_1,
  input  in_2,
  input  in_3,
  input  in_4,
  input  in_5,
  input  in_6,
  input  in_7,
  input  in_8,
  input  in_9,
  input  in_10,
  input  in_11,
  input  in_12,
  input  in_13,
  input  in_14,
  input  in_15,
  input  in_16,
  input  in_17,
  input  in_18,
  input  in_19,
  input  in_20,
  input  in_21,
  input  in_22,
  input  in_23,
  input  in_24,
  input  MANUAL,
  input  in_26,
  input  in_27,
  input  in_28,
  input  in_29,
  input  in_30,
  input  in_31,
  input  in_32,
  input  in_33,
  input  in_34,
  input  in_35,
  input  in_36,
  input  in_37,
  input  in_38,
  input  in_39,
  input  in_40,
  input  in_41,
  input  in_42,
  input  in_43,
  input  in_44,
  input  in_45,
  input  in_46,
  input  in_47,
  input  in_48,
  input  in_49,
  input  in_50,
  input  in_51,
  input  in_52,
  input  in_53,
  input  in_54,
  input  in_55,
  input  in_56,
  input  in_57,
  input  in_58,
  input  in_59,
  input  in_60,
  input  in_61,
  input  in_62,
  input  in_63,
  input  in_64,
  input  in_65,
  input  in_66,
  input  in_67,
  input  in_68,
  input  in_69,
  input  in_70,
  input  in_71,
  input  in_72,
  input  in_73,
  input  in_74,
  input  in_75,
  input  in_76,
  input  in_77,
  input  in_78,
  input  in_79,
  input  in_80,
  input  in_81,
  input  in_82,
  input  in_83,
  input  in_84,
  input  in_85,
  input  in_86,
  input  in_87,
  input  in_88,
  input  in_89,
  input  in_90,
  input  in_91,
  input  in_92,
  input  in_93,
  input  in_94,
  input  in_95,
  input  in_96,
  input  in_97,
  input  in_98,
  input  in_99,
  input  in_100,
  input  in_101,
  input  in_102,
  input  in_103,
  input  in_104,
  input  in_105,
  input  in_106,
  input  in_107,
  input  in_108,
  input  in_109,
  input  in_110,
  input  in_111,
  input  in_112,
  input  in_113,
  input  in_114,
  input  in_115,
  input  in_116,
  input  in_117,
  input  in_118,
  input  in_119,
  input  in_120,
  input  in_121,
  input  in_122,
  input  in_123,
  input  in_124,
  input  in_125,
  input  in_126,
  input  in_127,
  input  in_128,
  input  in_129,
  input  in_130,
  input  in_131,
  input  in_132,
  input  in_133,
  input  in_134,
  input  in_135,
  input  in_136,
  input  in_137,
  input  in_138,
  input  in_139,
  input  in_140,
  input  in_141,
  input  in_142,
  input  in_143,
  input  in_144,
  input  in_145,
  input  in_146,
  input  in_147,
  input  in_148,
  input  in_149,
  input  in_150,
  input  in_151,
  input  in_152,
  input  in_153,
  input  in_154,
  input  in_155,
  input  in_156,
  input  in_157,
  input  in_158,
  input  in_159,
  input  in_160,
  input  in_161,
  input  in_162,
  input  in_163,
  input  in_164,
  input  in_165,
  input  in_166,
  input  in_167,
  input  in_168,
  input  in_169,
  input  in_170,
  input  in_171,
  input  in_172,
  input  in_173,
  input  in_174,
  input  in_175,
  input  in_176,
  input  in_177,
  input  in_178,
  input  in_179,
  input  in_180,
  input  in_181,
  input  in_182,
  input  in_183,
  input  in_184,
  input  in_185,
  input  in_186,
  input  in_187,
  input  in_188,
  input  in_189,
  input  in_190,
  input  in_191,
  input  in_192,
  input  in_193
);

  wire and_1_out, and_2_out, and_3_out, and_4_out, and_5_out, and_6_out, and_7_out, and_8_out, M01, m01_t,
       M02, m02_t, M03, m03_t, M04, m04_t, M05, m05_t, M06, m06_t, M07, m07_t, M08, m08_t, M09, m09_t, M10,
       m10_t, M11, m11_t, M12, m12_t, M13, m13_t, M14, m14_t, M15, m15_t, M16, m16_t, M17, m17_t, M18, m18_t,
       M19, m19_t, M20, m20_t, M21, m21_t, M22, m22_t, M23, m23_t, M24, m24_t, M25, m25_t, M26, m26_t, M27,
       m27_t, M28, m28_t, M29, m29_t, M30, m30_t, M31, m31_t, M32, m32_t, M33, m33_t, M34, m34_t, M35, m35_t,
       M36, m36_t, M37, m37_t, M38, m38_t, M39, m39_t, M40, m40_t, M41, m41_t, M42, m42_t, M43, m43_t, M44,
       m44_t, M45, m45_t, M46, m46_t, M47, m47_t, M48, m48_t, M49, m49_t, M50, m50_t, M51, m51_t, M52, m52_t,
       M53, m53_t, M54, m54_t, M55, m55_t, M56, m56_t, M57, m57_t, M58, m58_t, M59, m59_t, M60, m60_t, M61,
       m61_t, M62, m62_t, M63, m63_t, M64, m64_t, NEW_GAME_out, S_M01, S_M02, S_M03, S_M04, S_M05, S_M06,
       S_M07, S_M08, S_M09, S_M10, S_M11, S_M12, S_M13, S_M14, S_M15, S_M16, S_M17, S_M18, S_M19, S_M20,
       S_M21, S_M22, S_M23, S_M24, S_M25, S_M26, S_M27, S_M28, S_M29, S_M30, S_M31, S_M32, S_M33, S_M34,
       S_M35, S_M36, S_M37, S_M38, S_M39, S_M40, S_M41, S_M42, S_M43, S_M44, S_M45, S_M46, S_M47, S_M48,
       S_M49, S_M50, S_M51, S_M52, S_M53, S_M54, S_M55, S_M56, S_M57, S_M58, S_M59, S_M60, S_M61, S_M62,
       S_M63, S_M64, SUCCESS;
  wire [3:0] D_M01, D_M02, D_M03, D_M04, D_M05, D_M06, D_M07, D_M08, D_M09, D_M10, D_M11, D_M12, D_M13,
       D_M14, D_M15, D_M16, D_M17, D_M18, D_M19, D_M20, D_M21, D_M22, D_M23, D_M24, D_M25, D_M26, D_M27,
       D_M28, D_M29, D_M30, D_M31, D_M32, D_M33, D_M34, D_M35, D_M36, D_M37, D_M38, D_M39, D_M40, D_M41,
       D_M42, D_M43, D_M44, D_M45, D_M46, D_M47, D_M48, D_M49, D_M50, D_M51, D_M52, D_M53, D_M54, D_M55,
       D_M56, D_M57, D_M58, D_M59, D_M60, D_M61, D_M62, D_M63, D_M64;
  wire [6:0] printsuccess_1_out2_2, printsuccess_1_out2_3, printsuccess_1_out2_4, printsuccess_1_out3_2,
       printsuccess_1_out3_3, printsuccess_1_out3_4, printsuccess_1_out4_2, printsuccess_1_out4_3,
       printsuccess_1_out4_4, printsuccess_1_out5_2, printsuccess_1_out5_3, printsuccess_1_out5_4,
       printsuccess_1_out6_2, printsuccess_1_out6_3, printsuccess_1_out6_4, printsuccess_1_out7_2,
       printsuccess_1_out7_3, printsuccess_1_out7_4;
  wire [13:0] printsuccess_1_out2, printsuccess_1_out3, printsuccess_1_out4, printsuccess_1_out5,
       printsuccess_1_out6, printsuccess_1_out7;
  wire [34:0] printsuccess_1_out1;
  wire [63:0] random_1_out;

  Random #(.width(64)) random_1 (.clk(NEW_GAME_out), .out(random_1_out));  // open: clr, next
  Button NEW_GAME (.out(NEW_GAME_out));
  MineControl minecontrol_1 (
    .E(M02), .SE(M10), .S(M09), .MINE_IN(m01_t), .TOUCH(in_2), .CHECK(in_1), .HEXDIGIT(D_M01),
    .MINE_OUT(M01), .SUCCESS(S_M01));  // open: N, NE, SW, W, NW
  MineControl minecontrol_2 (
    .N(M01), .NE(M02), .E(M10), .SE(M18), .S(M17), .MINE_IN(m09_t), .TOUCH(in_35), .CHECK(in_34),
    .HEXDIGIT(D_M09), .MINE_OUT(M09), .SUCCESS(S_M09));  // open: SW, W, NW
  MineControl minecontrol_3 (
    .N(M09), .NE(M10), .E(M18), .SE(M26), .S(M25), .MINE_IN(m17_t), .TOUCH(in_67), .CHECK(in_66),
    .HEXDIGIT(D_M17), .MINE_OUT(M17), .SUCCESS(S_M17));  // open: SW, W, NW
  MineControl minecontrol_4 (
    .N(M17), .NE(M18), .E(M26), .SE(M34), .S(M33), .MINE_IN(m25_t), .TOUCH(in_91), .CHECK(in_90),
    .HEXDIGIT(D_M25), .MINE_OUT(M25), .SUCCESS(S_M25));  // open: SW, W, NW
  MineControl minecontrol_5 (
    .N(M25), .NE(M26), .E(M34), .SE(M42), .S(M41), .MINE_IN(m33_t), .TOUCH(in_123), .CHECK(in_122),
    .HEXDIGIT(D_M33), .MINE_OUT(M33), .SUCCESS(S_M33));  // open: SW, W, NW
  MineControl minecontrol_6 (
    .N(M33), .NE(M34), .E(M42), .SE(M50), .S(M49), .MINE_IN(m41_t), .TOUCH(in_147), .CHECK(in_146),
    .HEXDIGIT(D_M41), .MINE_OUT(M41), .SUCCESS(S_M41));  // open: SW, W, NW
  MineControl minecontrol_7 (
    .N(M41), .NE(M42), .E(M50), .SE(M58), .S(M57), .MINE_IN(m49_t), .TOUCH(in_163), .CHECK(in_162),
    .HEXDIGIT(D_M49), .MINE_OUT(M49), .SUCCESS(S_M49));  // open: SW, W, NW
  MineControl minecontrol_8 (
    .N(M49), .NE(M50), .E(M58), .MINE_IN(m57_t), .TOUCH(in_179), .CHECK(in_178), .HEXDIGIT(D_M57),
    .MINE_OUT(M57), .SUCCESS(S_M57));  // open: SE, S, SW, W, NW
  and and_1 (and_1_out, S_M01, S_M02, S_M03, S_M04, S_M05, S_M06, S_M07, S_M08);
  and and_2 (and_2_out, S_M09, S_M10, S_M11, S_M12, S_M13, S_M14, S_M15, S_M16);
  and and_3 (and_3_out, S_M17, S_M18, S_M19, S_M20, S_M21, S_M22, S_M23, S_M24);
  and and_4 (and_4_out, S_M25, S_M26, S_M27, S_M28, S_M29, S_M30, S_M31, S_M32);
  and and_5 (and_5_out, S_M33, S_M34, S_M35, S_M36, S_M37, S_M38, S_M39, S_M40);
  and and_6 (and_6_out, S_M41, S_M42, S_M43, S_M44, S_M45, S_M46, S_M47, S_M48);
  and and_7 (and_7_out, S_M49, S_M50, S_M51, S_M52, S_M53, S_M54, S_M55, S_M56);
  and and_8 (and_8_out, S_M57, S_M58, S_M59, S_M60, S_M61, S_M62, S_M63, S_M64);
  and and_9 (SUCCESS, and_1_out, and_2_out, and_3_out, and_4_out, and_5_out, and_6_out, and_7_out, and_8_out);
  Multiplexer #(.width(64)) multiplexer_1 (
    .in0(random_1_out),
    .in1({in_145, in_144, in_143, in_142, in_141, in_140, in_139, in_138, in_121, in_120, in_119, in_118, in_117, in_116, in_115, in_114, in_113, in_112, in_111, in_110, in_109, in_108, in_107, in_106, in_89, in_88, in_87, in_86, in_85, in_84, in_83, in_82, in_65, in_64, in_63, in_62, in_61, in_60, in_59, in_58, in_57, in_56, in_55, in_54, in_53, in_52, in_51, in_50, in_33, in_32, in_31, in_30, in_29, in_28, in_27, in_26, in_24, in_23, in_22, in_21, in_20, in_19, in_18, in_17}),
    .out({m64_t, m63_t, m62_t, m61_t, m60_t, m59_t, m58_t, m57_t, m56_t, m55_t, m54_t, m53_t, m52_t, m51_t, m50_t, m49_t, m48_t, m47_t, m46_t, m45_t, m44_t, m43_t, m42_t, m41_t, m40_t, m39_t, m38_t, m37_t, m36_t, m35_t, m34_t, m33_t, m32_t, m31_t, m30_t, m29_t, m28_t, m27_t, m26_t, m25_t, m24_t, m23_t, m22_t, m21_t, m20_t, m19_t, m18_t, m17_t, m16_t, m15_t, m14_t, m13_t, m12_t, m11_t, m10_t, m09_t, m08_t, m07_t, m06_t, m05_t, m04_t, m03_t, m02_t, m01_t}),
    .sel(MANUAL));
  MineControl minecontrol_9 (
    .E(M03), .SE(M11), .S(M10), .SW(M09), .W(M01), .MINE_IN(m02_t), .TOUCH(in_4), .CHECK(in_3),
    .HEXDIGIT(D_M02), .MINE_OUT(M02), .SUCCESS(S_M02));  // open: N, NE, NW
  MineControl minecontrol_10 (
    .N(M02), .NE(M03), .E(M11), .SE(M19), .S(M18), .SW(M17), .W(M09), .NW(M01), .MINE_IN(m10_t),
    .TOUCH(in_37), .CHECK(in_36), .HEXDIGIT(D_M10), .MINE_OUT(M10), .SUCCESS(S_M10));
  MineControl minecontrol_11 (
    .N(M10), .NE(M11), .E(M19), .SE(M27), .S(M26), .SW(M25), .W(M17), .NW(M09), .MINE_IN(m18_t),
    .TOUCH(in_69), .CHECK(in_68), .HEXDIGIT(D_M18), .MINE_OUT(M18), .SUCCESS(S_M18));
  MineControl minecontrol_12 (
    .N(M18), .NE(M19), .E(M27), .SE(M35), .S(M34), .SW(M33), .W(M25), .NW(M17), .MINE_IN(m26_t),
    .TOUCH(in_93), .CHECK(in_92), .HEXDIGIT(D_M26), .MINE_OUT(M26), .SUCCESS(S_M26));
  MineControl minecontrol_13 (
    .N(M26), .NE(M27), .E(M35), .SE(M43), .S(M42), .SW(M41), .W(M33), .NW(M25), .MINE_IN(m34_t),
    .TOUCH(in_125), .CHECK(in_124), .HEXDIGIT(D_M34), .MINE_OUT(M34), .SUCCESS(S_M34));
  MineControl minecontrol_14 (
    .N(M34), .NE(M35), .E(M43), .SE(M51), .S(M50), .SW(M49), .W(M41), .NW(M33), .MINE_IN(m42_t),
    .TOUCH(in_149), .CHECK(in_148), .HEXDIGIT(D_M42), .MINE_OUT(M42), .SUCCESS(S_M42));
  MineControl minecontrol_15 (
    .N(M42), .NE(M43), .E(M51), .SE(M59), .S(M58), .SW(M57), .W(M49), .NW(M41), .MINE_IN(m50_t),
    .TOUCH(in_165), .CHECK(in_164), .HEXDIGIT(D_M50), .MINE_OUT(M50), .SUCCESS(S_M50));
  MineControl minecontrol_16 (
    .N(M50), .NE(M51), .E(M59), .W(M57), .NW(M49), .MINE_IN(m58_t), .TOUCH(in_181), .CHECK(in_180),
    .HEXDIGIT(D_M58), .MINE_OUT(M58), .SUCCESS(S_M58));  // open: SE, S, SW
  MineControl minecontrol_17 (
    .E(M04), .SE(M12), .S(M11), .SW(M10), .W(M02), .MINE_IN(m03_t), .TOUCH(in_6), .CHECK(in_5),
    .HEXDIGIT(D_M03), .MINE_OUT(M03), .SUCCESS(S_M03));  // open: N, NE, NW
  MineControl minecontrol_18 (
    .N(M03), .NE(M04), .E(M12), .SE(M20), .S(M19), .SW(M18), .W(M10), .NW(M02), .MINE_IN(m11_t),
    .TOUCH(in_39), .CHECK(in_38), .HEXDIGIT(D_M11), .MINE_OUT(M11), .SUCCESS(S_M11));
  MineControl minecontrol_19 (
    .N(M11), .NE(M12), .E(M20), .SE(M28), .S(M27), .SW(M26), .W(M18), .NW(M10), .MINE_IN(m19_t),
    .TOUCH(in_71), .CHECK(in_70), .HEXDIGIT(D_M19), .MINE_OUT(M19), .SUCCESS(S_M19));
  MineControl minecontrol_20 (
    .N(M19), .NE(M20), .E(M28), .SE(M36), .S(M35), .SW(M34), .W(M26), .NW(M18), .MINE_IN(m27_t),
    .TOUCH(in_95), .CHECK(in_94), .HEXDIGIT(D_M27), .MINE_OUT(M27), .SUCCESS(S_M27));
  MineControl minecontrol_21 (
    .N(M27), .NE(M28), .E(M36), .SE(M44), .S(M43), .SW(M42), .W(M34), .NW(M26), .MINE_IN(m35_t),
    .TOUCH(in_127), .CHECK(in_126), .HEXDIGIT(D_M35), .MINE_OUT(M35), .SUCCESS(S_M35));
  MineControl minecontrol_22 (
    .N(M35), .NE(M36), .E(M44), .SE(M52), .S(M51), .SW(M50), .W(M42), .NW(M34), .MINE_IN(m43_t),
    .TOUCH(in_151), .CHECK(in_150), .HEXDIGIT(D_M43), .MINE_OUT(M43), .SUCCESS(S_M43));
  MineControl minecontrol_23 (
    .N(M43), .NE(M44), .E(M52), .SE(M60), .S(M59), .SW(M58), .W(M50), .NW(M42), .MINE_IN(m51_t),
    .TOUCH(in_167), .CHECK(in_166), .HEXDIGIT(D_M51), .MINE_OUT(M51), .SUCCESS(S_M51));
  MineControl minecontrol_24 (
    .N(M51), .NE(M52), .E(M60), .W(M58), .NW(M50), .MINE_IN(m59_t), .TOUCH(in_183), .CHECK(in_182),
    .HEXDIGIT(D_M59), .MINE_OUT(M59), .SUCCESS(S_M59));  // open: SE, S, SW
  Hex_Digit_Display hex_digit_display_1 (.value(D_M01));  // open: dp
  Hex_Digit_Display hex_digit_display_2 (.value(D_M09));  // open: dp
  Hex_Digit_Display hex_digit_display_3 (.value(D_M17));  // open: dp
  Hex_Digit_Display hex_digit_display_4 (.value(D_M25));  // open: dp
  Hex_Digit_Display hex_digit_display_5 (.value(D_M33));  // open: dp
  Hex_Digit_Display hex_digit_display_6 (.value(D_M41));  // open: dp
  Hex_Digit_Display hex_digit_display_7 (.value(D_M49));  // open: dp
  Hex_Digit_Display hex_digit_display_8 (.value(D_M57));  // open: dp
  MineControl minecontrol_25 (
    .E(M05), .SE(M13), .S(M12), .SW(M11), .W(M03), .MINE_IN(m04_t), .TOUCH(in_8), .CHECK(in_7),
    .HEXDIGIT(D_M04), .MINE_OUT(M04), .SUCCESS(S_M04));  // open: N, NE, NW
  MineControl minecontrol_26 (
    .N(M04), .NE(M05), .E(M13), .SE(M21), .S(M20), .SW(M19), .W(M11), .NW(M03), .MINE_IN(m12_t),
    .TOUCH(in_41), .CHECK(in_40), .HEXDIGIT(D_M12), .MINE_OUT(M12), .SUCCESS(S_M12));
  MineControl minecontrol_27 (
    .N(M12), .NE(M13), .E(M21), .SE(M29), .S(M28), .SW(M27), .W(M19), .NW(M11), .MINE_IN(m20_t),
    .TOUCH(in_73), .CHECK(in_72), .HEXDIGIT(D_M20), .MINE_OUT(M20), .SUCCESS(S_M20));
  MineControl minecontrol_28 (
    .N(M20), .NE(M21), .E(M29), .SE(M37), .S(M36), .SW(M35), .W(M27), .NW(M19), .MINE_IN(m28_t),
    .TOUCH(in_97), .CHECK(in_96), .HEXDIGIT(D_M28), .MINE_OUT(M28), .SUCCESS(S_M28));
  MineControl minecontrol_29 (
    .N(M28), .NE(M29), .E(M37), .SE(M45), .S(M44), .SW(M43), .W(M35), .NW(M27), .MINE_IN(m36_t),
    .TOUCH(in_129), .CHECK(in_128), .HEXDIGIT(D_M36), .MINE_OUT(M36), .SUCCESS(S_M36));
  MineControl minecontrol_30 (
    .N(M36), .NE(M37), .E(M45), .SE(M53), .S(M52), .SW(M51), .W(M43), .NW(M35), .MINE_IN(m44_t),
    .TOUCH(in_153), .CHECK(in_152), .HEXDIGIT(D_M44), .MINE_OUT(M44), .SUCCESS(S_M44));
  MineControl minecontrol_31 (
    .N(M44), .NE(M45), .E(M53), .SE(M61), .S(M60), .SW(M59), .W(M51), .NW(M43), .MINE_IN(m52_t),
    .TOUCH(in_169), .CHECK(in_168), .HEXDIGIT(D_M52), .MINE_OUT(M52), .SUCCESS(S_M52));
  MineControl minecontrol_32 (
    .N(M52), .NE(M53), .E(M61), .W(M59), .NW(M51), .MINE_IN(m60_t), .TOUCH(in_185), .CHECK(in_184),
    .HEXDIGIT(D_M60), .MINE_OUT(M60), .SUCCESS(S_M60));  // open: SE, S, SW
  Hex_Digit_Display hex_digit_display_9 (.value(D_M02));  // open: dp
  Hex_Digit_Display hex_digit_display_10 (.value(D_M10));  // open: dp
  Hex_Digit_Display hex_digit_display_11 (.value(D_M18));  // open: dp
  Hex_Digit_Display hex_digit_display_12 (.value(D_M26));  // open: dp
  Hex_Digit_Display hex_digit_display_13 (.value(D_M34));  // open: dp
  Hex_Digit_Display hex_digit_display_14 (.value(D_M42));  // open: dp
  Hex_Digit_Display hex_digit_display_15 (.value(D_M50));  // open: dp
  Hex_Digit_Display hex_digit_display_16 (.value(D_M58));  // open: dp
  PrintSuccess printsuccess_1 (
    .SUCCESS(SUCCESS), .OUT1(printsuccess_1_out1),
    .OUT2({printsuccess_1_out2_4, printsuccess_1_out2_3, printsuccess_1_out2_2, printsuccess_1_out2}),
    .OUT3({printsuccess_1_out3_4, printsuccess_1_out3_3, printsuccess_1_out3_2, printsuccess_1_out3}),
    .OUT4({printsuccess_1_out4_4, printsuccess_1_out4_3, printsuccess_1_out4_2, printsuccess_1_out4}),
    .OUT5({printsuccess_1_out5_4, printsuccess_1_out5_3, printsuccess_1_out5_2, printsuccess_1_out5}),
    .OUT6({printsuccess_1_out6_4, printsuccess_1_out6_3, printsuccess_1_out6_2, printsuccess_1_out6}),
    .OUT7({printsuccess_1_out7_4, printsuccess_1_out7_3, printsuccess_1_out7_2, printsuccess_1_out7}));
  Hex_Digit_Display hex_digit_display_17 (.value(D_M03));  // open: dp
  Hex_Digit_Display hex_digit_display_18 (.value(D_M11));  // open: dp
  Hex_Digit_Display hex_digit_display_19 (.value(D_M19));  // open: dp
  Hex_Digit_Display hex_digit_display_20 (.value(D_M27));  // open: dp
  Hex_Digit_Display hex_digit_display_21 (.value(D_M35));  // open: dp
  Hex_Digit_Display hex_digit_display_22 (.value(D_M43));  // open: dp
  Hex_Digit_Display hex_digit_display_23 (.value(D_M51));  // open: dp
  Hex_Digit_Display hex_digit_display_24 (.value(D_M59));  // open: dp
  DotMatrix #(.matrixcols(41)) dotmatrix_1 (
    .col0(printsuccess_1_out1[34:28]), .col1(printsuccess_1_out1[27:21]), .col2(printsuccess_1_out1[20:14]),
    .col3(printsuccess_1_out1[13:7]), .col4(printsuccess_1_out1[6:0]), .col5({7{1'b0}}),
    .col6(printsuccess_1_out2_4), .col7(printsuccess_1_out2_3), .col8(printsuccess_1_out2_2),
    .col9(printsuccess_1_out2[13:7]), .col10(printsuccess_1_out2[6:0]), .col11({7{1'b0}}),
    .col12(printsuccess_1_out3_4), .col13(printsuccess_1_out3_3), .col14(printsuccess_1_out3_2),
    .col15(printsuccess_1_out3[13:7]), .col16(printsuccess_1_out3[6:0]), .col17({7{1'b0}}),
    .col18(printsuccess_1_out4_4), .col19(printsuccess_1_out4_3), .col20(printsuccess_1_out4_2),
    .col21(printsuccess_1_out4[13:7]), .col22(printsuccess_1_out4[6:0]), .col23({7{1'b0}}),
    .col24(printsuccess_1_out5_4), .col25(printsuccess_1_out5_3), .col26(printsuccess_1_out5_2),
    .col27(printsuccess_1_out5[13:7]), .col28(printsuccess_1_out5[6:0]), .col29({7{1'b0}}),
    .col30(printsuccess_1_out6_4), .col31(printsuccess_1_out6_3), .col32(printsuccess_1_out6_2),
    .col33(printsuccess_1_out6[13:7]), .col34(printsuccess_1_out6[6:0]), .col35({7{1'b0}}),
    .col36(printsuccess_1_out7_4), .col37(printsuccess_1_out7_3), .col38(printsuccess_1_out7_2),
    .col39(printsuccess_1_out7[13:7]), .col40(printsuccess_1_out7[6:0]));
  Hex_Digit_Display hex_digit_display_25 (.value(D_M04));  // open: dp
  Hex_Digit_Display hex_digit_display_26 (.value(D_M12));  // open: dp
  Hex_Digit_Display hex_digit_display_27 (.value(D_M20));  // open: dp
  Hex_Digit_Display hex_digit_display_28 (.value(D_M28));  // open: dp
  Hex_Digit_Display hex_digit_display_29 (.value(D_M36));  // open: dp
  Hex_Digit_Display hex_digit_display_30 (.value(D_M44));  // open: dp
  Hex_Digit_Display hex_digit_display_31 (.value(D_M52));  // open: dp
  Hex_Digit_Display hex_digit_display_32 (.value(D_M60));  // open: dp
  MineControl minecontrol_33 (
    .E(M06), .SE(M14), .S(M13), .SW(M12), .W(M04), .MINE_IN(m05_t), .TOUCH(in_10), .CHECK(in_9),
    .HEXDIGIT(D_M05), .MINE_OUT(M05), .SUCCESS(S_M05));  // open: N, NE, NW
  MineControl minecontrol_34 (
    .N(M05), .NE(M06), .E(M14), .SE(M22), .S(M21), .SW(M20), .W(M12), .NW(M04), .MINE_IN(m13_t),
    .TOUCH(in_43), .CHECK(in_42), .HEXDIGIT(D_M13), .MINE_OUT(M13), .SUCCESS(S_M13));
  MineControl minecontrol_35 (
    .N(M13), .NE(M14), .E(M22), .SE(M30), .S(M29), .SW(M28), .W(M20), .NW(M12), .MINE_IN(m21_t),
    .TOUCH(in_75), .CHECK(in_74), .HEXDIGIT(D_M21), .MINE_OUT(M21), .SUCCESS(S_M21));
  MineControl minecontrol_36 (
    .N(M21), .NE(M22), .E(M30), .SE(M38), .S(M37), .SW(M36), .W(M28), .NW(M20), .MINE_IN(m29_t),
    .TOUCH(in_99), .CHECK(in_98), .HEXDIGIT(D_M29), .MINE_OUT(M29), .SUCCESS(S_M29));
  MineControl minecontrol_37 (
    .N(M29), .NE(M30), .E(M38), .SE(M46), .S(M45), .SW(M44), .W(M36), .NW(M28), .MINE_IN(m37_t),
    .TOUCH(in_131), .CHECK(in_130), .HEXDIGIT(D_M37), .MINE_OUT(M37), .SUCCESS(S_M37));
  MineControl minecontrol_38 (
    .N(M37), .NE(M38), .E(M46), .SE(M54), .S(M53), .SW(M54), .W(M44), .NW(M36), .MINE_IN(m45_t),
    .TOUCH(in_155), .CHECK(in_154), .HEXDIGIT(D_M45), .MINE_OUT(M45), .SUCCESS(S_M45));
  MineControl minecontrol_39 (
    .N(M45), .NE(M46), .E(M54), .SE(M62), .S(M61), .SW(M60), .W(M52), .NW(M44), .MINE_IN(m53_t),
    .TOUCH(in_171), .CHECK(in_170), .HEXDIGIT(D_M53), .MINE_OUT(M53), .SUCCESS(S_M53));
  MineControl minecontrol_40 (
    .N(M53), .NE(M54), .E(M62), .W(M60), .NW(M52), .MINE_IN(m61_t), .TOUCH(in_187), .CHECK(in_186),
    .HEXDIGIT(D_M61), .MINE_OUT(M61), .SUCCESS(S_M61));  // open: SE, S, SW
  Hex_Digit_Display hex_digit_display_33 (.value(D_M05));  // open: dp
  Hex_Digit_Display hex_digit_display_34 (.value(D_M13));  // open: dp
  Hex_Digit_Display hex_digit_display_35 (.value(D_M21));  // open: dp
  Hex_Digit_Display hex_digit_display_36 (.value(D_M29));  // open: dp
  Hex_Digit_Display hex_digit_display_37 (.value(D_M37));  // open: dp
  Hex_Digit_Display hex_digit_display_38 (.value(D_M45));  // open: dp
  Hex_Digit_Display hex_digit_display_39 (.value(D_M53));  // open: dp
  Hex_Digit_Display hex_digit_display_40 (.value(D_M61));  // open: dp
  Hex_Digit_Display hex_digit_display_41 (.value(D_M06));  // open: dp
  Hex_Digit_Display hex_digit_display_42 (.value(D_M14));  // open: dp
  Hex_Digit_Display hex_digit_display_43 (.value(D_M22));  // open: dp
  Hex_Digit_Display hex_digit_display_44 (.value(D_M30));  // open: dp
  Hex_Digit_Display hex_digit_display_45 (.value(D_M38));  // open: dp
  Hex_Digit_Display hex_digit_display_46 (.value(D_M46));  // open: dp
  Hex_Digit_Display hex_digit_display_47 (.value(D_M54));  // open: dp
  Hex_Digit_Display hex_digit_display_48 (.value(D_M62));  // open: dp
  Hex_Digit_Display hex_digit_display_49 (.value(D_M07));  // open: dp
  Hex_Digit_Display hex_digit_display_50 (.value(D_M15));  // open: dp
  Hex_Digit_Display hex_digit_display_51 (.value(D_M23));  // open: dp
  Hex_Digit_Display hex_digit_display_52 (.value(D_M31));  // open: dp
  Hex_Digit_Display hex_digit_display_53 (.value(D_M39));  // open: dp
  Hex_Digit_Display hex_digit_display_54 (.value(D_M47));  // open: dp
  Hex_Digit_Display hex_digit_display_55 (.value(D_M55));  // open: dp
  Hex_Digit_Display hex_digit_display_56 (.value(D_M63));  // open: dp
  Hex_Digit_Display hex_digit_display_57 (.value(D_M08));  // open: dp
  Hex_Digit_Display hex_digit_display_58 (.value(D_M16));  // open: dp
  Hex_Digit_Display hex_digit_display_59 (.value(D_M24));  // open: dp
  Hex_Digit_Display hex_digit_display_60 (.value(D_M32));  // open: dp
  Hex_Digit_Display hex_digit_display_61 (.value(D_M40));  // open: dp
  Hex_Digit_Display hex_digit_display_62 (.value(D_M48));  // open: dp
  Hex_Digit_Display hex_digit_display_63 (.value(D_M56));  // open: dp
  Hex_Digit_Display hex_digit_display_64 (.value(D_M64));  // open: dp
  MineControl minecontrol_41 (
    .E(M07), .SE(M15), .S(M14), .SW(M13), .W(M05), .MINE_IN(m06_t), .TOUCH(in_12), .CHECK(in_11),
    .HEXDIGIT(D_M06), .MINE_OUT(M06), .SUCCESS(S_M06));  // open: N, NE, NW
  MineControl minecontrol_42 (
    .N(M06), .NE(M07), .E(M15), .SE(M23), .S(M22), .SW(M21), .W(M13), .NW(M05), .MINE_IN(m14_t),
    .TOUCH(in_45), .CHECK(in_44), .HEXDIGIT(D_M14), .MINE_OUT(M14), .SUCCESS(S_M14));
  MineControl minecontrol_43 (
    .N(M14), .NE(M15), .E(M23), .SE(M31), .S(M30), .SW(M29), .W(M21), .NW(M13), .MINE_IN(m22_t),
    .TOUCH(in_77), .CHECK(in_76), .HEXDIGIT(D_M22), .MINE_OUT(M22), .SUCCESS(S_M22));
  MineControl minecontrol_44 (
    .N(M22), .NE(M23), .E(M31), .SE(M39), .S(M38), .SW(M37), .W(M29), .NW(M21), .MINE_IN(m30_t),
    .TOUCH(in_101), .CHECK(in_100), .HEXDIGIT(D_M30), .MINE_OUT(M30), .SUCCESS(S_M30));
  MineControl minecontrol_45 (
    .N(M30), .NE(M31), .E(M39), .SE(M47), .S(M46), .SW(M45), .W(M37), .NW(M29), .MINE_IN(m38_t),
    .TOUCH(in_133), .CHECK(in_132), .HEXDIGIT(D_M38), .MINE_OUT(M38), .SUCCESS(S_M38));
  MineControl minecontrol_46 (
    .N(M38), .NE(M39), .E(M47), .SE(M55), .S(M54), .SW(M53), .W(M45), .NW(M37), .MINE_IN(m46_t),
    .TOUCH(in_157), .CHECK(in_156), .HEXDIGIT(D_M46), .MINE_OUT(M46), .SUCCESS(S_M46));
  MineControl minecontrol_47 (
    .N(M46), .NE(M47), .E(M55), .SE(M63), .S(M62), .SW(M61), .W(M53), .NW(M45), .MINE_IN(m54_t),
    .TOUCH(in_173), .CHECK(in_172), .HEXDIGIT(D_M54), .MINE_OUT(M54), .SUCCESS(S_M54));
  MineControl minecontrol_48 (
    .N(M54), .NE(M55), .E(M63), .W(M61), .NW(M53), .MINE_IN(m62_t), .TOUCH(in_189), .CHECK(in_188),
    .HEXDIGIT(D_M62), .MINE_OUT(M62), .SUCCESS(S_M62));  // open: SE, S, SW
  MineControl minecontrol_49 (
    .E(M08), .SE(M16), .S(M15), .SW(M14), .W(M06), .MINE_IN(m07_t), .TOUCH(in_14), .CHECK(in_13),
    .HEXDIGIT(D_M07), .MINE_OUT(M07), .SUCCESS(S_M07));  // open: N, NE, NW
  MineControl minecontrol_50 (
    .N(M07), .NE(M08), .E(M16), .SE(M24), .S(M23), .SW(M22), .W(M14), .NW(M06), .MINE_IN(m15_t),
    .TOUCH(in_47), .CHECK(in_46), .HEXDIGIT(D_M15), .MINE_OUT(M15), .SUCCESS(S_M15));
  MineControl minecontrol_51 (
    .N(M15), .NE(M16), .E(M24), .SE(M32), .S(M31), .SW(M30), .W(M22), .NW(M14), .MINE_IN(m23_t),
    .TOUCH(in_79), .CHECK(in_78), .HEXDIGIT(D_M23), .MINE_OUT(M23), .SUCCESS(S_M23));
  MineControl minecontrol_52 (
    .N(M23), .NE(M24), .E(M32), .SE(M40), .S(M39), .SW(M38), .W(M30), .NW(M22), .MINE_IN(m31_t),
    .TOUCH(in_103), .CHECK(in_102), .HEXDIGIT(D_M31), .MINE_OUT(M31), .SUCCESS(S_M31));
  MineControl minecontrol_53 (
    .N(M31), .NE(M32), .E(M40), .SE(M48), .S(M47), .SW(M46), .W(M38), .NW(M30), .MINE_IN(m39_t),
    .TOUCH(in_135), .CHECK(in_134), .HEXDIGIT(D_M39), .MINE_OUT(M39), .SUCCESS(S_M39));
  MineControl minecontrol_54 (
    .N(M39), .NE(M40), .E(M48), .SE(M56), .S(M55), .SW(M54), .W(M46), .NW(M38), .MINE_IN(m47_t),
    .TOUCH(in_159), .CHECK(in_158), .HEXDIGIT(D_M47), .MINE_OUT(M47), .SUCCESS(S_M47));
  MineControl minecontrol_55 (
    .N(M47), .NE(M48), .E(M56), .SE(M64), .S(M63), .SW(M62), .W(M54), .NW(M46), .MINE_IN(m55_t),
    .TOUCH(in_175), .CHECK(in_174), .HEXDIGIT(D_M55), .MINE_OUT(M55), .SUCCESS(S_M55));
  MineControl minecontrol_56 (
    .N(M55), .NE(M56), .E(M64), .W(M62), .NW(M54), .MINE_IN(m63_t), .TOUCH(in_191), .CHECK(in_190),
    .HEXDIGIT(D_M63), .MINE_OUT(M63), .SUCCESS(S_M63));  // open: SE, S, SW
  MineControl minecontrol_57 (
    .S(M16), .SW(M15), .W(M07), .MINE_IN(m08_t), .TOUCH(in_16), .CHECK(in_15), .HEXDIGIT(D_M08),
    .MINE_OUT(M08), .SUCCESS(S_M08));  // open: N, NE, E, SE, NW
  MineControl minecontrol_58 (
    .N(M08), .S(M24), .SW(M23), .W(M15), .NW(M07), .MINE_IN(m16_t), .TOUCH(in_49), .CHECK(in_48),
    .HEXDIGIT(D_M16), .MINE_OUT(M16), .SUCCESS(S_M16));  // open: NE, E, SE
  MineControl minecontrol_59 (
    .N(M16), .S(M32), .SW(M31), .W(M23), .NW(M15), .MINE_IN(m24_t), .TOUCH(in_81), .CHECK(in_80),
    .HEXDIGIT(D_M24), .MINE_OUT(M24), .SUCCESS(S_M24));  // open: NE, E, SE
  MineControl minecontrol_60 (
    .N(M24), .S(M40), .SW(M39), .W(M31), .NW(M23), .MINE_IN(m32_t), .TOUCH(in_105), .CHECK(in_104),
    .HEXDIGIT(D_M32), .MINE_OUT(M32), .SUCCESS(S_M32));  // open: NE, E, SE
  MineControl minecontrol_61 (
    .N(M32), .S(M48), .SW(M47), .W(M39), .NW(M31), .MINE_IN(m40_t), .TOUCH(in_137), .CHECK(in_136),
    .HEXDIGIT(D_M40), .MINE_OUT(M40), .SUCCESS(S_M40));  // open: NE, E, SE
  MineControl minecontrol_62 (
    .N(M40), .S(M56), .SW(M55), .W(M47), .NW(M39), .MINE_IN(m48_t), .TOUCH(in_161), .CHECK(in_160),
    .HEXDIGIT(D_M48), .MINE_OUT(M48), .SUCCESS(S_M48));  // open: NE, E, SE
  MineControl minecontrol_63 (
    .N(M48), .S(M64), .SW(M63), .W(M55), .NW(M47), .MINE_IN(m56_t), .TOUCH(in_177), .CHECK(in_176),
    .HEXDIGIT(D_M56), .MINE_OUT(M56), .SUCCESS(S_M56));  // open: NE, E, SE
  MineControl minecontrol_64 (
    .N(M56), .W(M63), .NW(M55), .MINE_IN(m64_t), .TOUCH(in_193), .CHECK(in_192), .HEXDIGIT(D_M64),
    .MINE_OUT(M64), .SUCCESS(S_M64));  // open: NE, E, SE, S, SW

  // Other names for the same wires on the sheet: C_M01 = in_1; C_M02 = in_3; C_M03 = in_5; C_M04 = in_7; C_M05 = in_9;
  //   C_M06 = in_11; C_M07 = in_13; C_M08 = in_15; C_M09 = in_34; C_M10 = in_36; C_M11 = in_38; C_M12 = in_40;
  //   C_M13 = in_42; C_M14 = in_44; C_M15 = in_46; C_M16 = in_48; C_M17 = in_66; C_M18 = in_68; C_M19 = in_70;
  //   C_M20 = in_72; C_M21 = in_74; C_M22 = in_76; C_M23 = in_78; C_M24 = in_80; C_M25 = in_90; C_M26 = in_92;
  //   C_M27 = in_94; C_M28 = in_96; C_M29 = in_98; C_M30 = in_100; C_M31 = in_102; C_M32 = in_104; C_M33 = in_122;
  //   C_M34 = in_124; C_M35 = in_126; C_M36 = in_128; C_M37 = in_130; C_M38 = in_132; C_M39 = in_134; C_M40 = in_136;
  //   C_M41 = in_146; C_M42 = in_148; C_M43 = in_150; C_M44 = in_152; C_M45 = in_154; C_M46 = in_156; C_M47 = in_158;
  //   C_M48 = in_160; C_M49 = in_162; C_M50 = in_164; C_M51 = in_166; C_M52 = in_168; C_M53 = in_170; C_M54 = in_172;
  //   C_M55 = in_174; C_M56 = in_176; C_M57 = in_178; C_M58 = in_180; C_M59 = in_182; C_M60 = in_184; C_M61 = in_186;
  //   C_M62 = in_188; C_M63 = in_190; C_M64 = in_192; T_M01 = in_2; T_M02 = in_4; T_M03 = in_6; T_M04 = in_8;
  //   T_M05 = in_10; T_M06 = in_12; T_M07 = in_14; T_M08 = in_16; T_M09 = in_35; T_M10 = in_37; T_M11 = in_39;
  //   T_M12 = in_41; T_M13 = in_43; T_M14 = in_45; T_M15 = in_47; T_M16 = in_49; T_M17 = in_67; T_M18 = in_69;
  //   T_M19 = in_71; T_M20 = in_73; T_M21 = in_75; T_M22 = in_77; T_M23 = in_79; T_M24 = in_81; T_M25 = in_91;
  //   T_M26 = in_93; T_M27 = in_95; T_M28 = in_97; T_M29 = in_99; T_M30 = in_101; T_M31 = in_103; T_M32 = in_105;
  //   T_M33 = in_123; T_M34 = in_125; T_M35 = in_127; T_M36 = in_129; T_M37 = in_131; T_M38 = in_133; T_M39 = in_135;
  //   T_M40 = in_137; T_M41 = in_147; T_M42 = in_149; T_M43 = in_151; T_M44 = in_153; T_M45 = in_155; T_M46 = in_157;
  //   T_M47 = in_159; T_M48 = in_161; T_M49 = in_163; T_M50 = in_165; T_M51 = in_167; T_M52 = in_169; T_M53 = in_171;
  //   T_M54 = in_173; T_M55 = in_175; T_M56 = in_177; T_M57 = in_179; T_M58 = in_181; T_M59 = in_183; T_M60 = in_185;
  //   T_M61 = in_187; T_M62 = in_189; T_M63 = in_191; T_M64 = in_193

  // Notes on the sheet:
  //   !MANUAL = 랜덤
  //   MANUAL = 수동
  //   C_M00 = Check M00
  //   T_M00 = Touch M00
  //   21101195 신용준
  //   IF you Check all the mine you will Succeed!!
endmodule

module MineControl (
  input  N,
  input  NE,
  input  E,
  input  SE,
  input  S,
  input  SW,
  input  W,
  input  NW,
  input  MINE_IN,
  input  TOUCH,
  input  CHECK,
  output [3:0] HEXDIGIT,
  output MINE_OUT,
  output SUCCESS
);

  wire [3:0] adder_1_out, adder_2_out, adder_3_out, adder_4_out, adder_5_out, adder_6_out, adder_7_out,
       bit_extender_1_out, bit_extender_2_out, bit_extender_3_out, bit_extender_4_out, bit_extender_5_out,
       bit_extender_6_out, bit_extender_7_out, bit_extender_8_out, multiplexer_1_out, multiplexer_2_out;

  assign bit_extender_1_out = {{3{1'b0}}, N};  // Bit_Extender bit_extender_1
  assign bit_extender_2_out = {{3{1'b0}}, NE};  // Bit_Extender bit_extender_2
  assign bit_extender_3_out = {{3{1'b0}}, E};  // Bit_Extender bit_extender_3
  assign bit_extender_4_out = {{3{1'b0}}, SE};  // Bit_Extender bit_extender_4
  assign bit_extender_5_out = {{3{1'b0}}, S};  // Bit_Extender bit_extender_5
  assign bit_extender_6_out = {{3{1'b0}}, SW};  // Bit_Extender bit_extender_6
  assign bit_extender_7_out = {{3{1'b0}}, W};  // Bit_Extender bit_extender_7
  assign bit_extender_8_out = {{3{1'b0}}, NW};  // Bit_Extender bit_extender_8
  Adder #(.width(4)) adder_1 (.a(bit_extender_1_out), .b(bit_extender_2_out), .out(adder_1_out));  // open: cin, cout
  Adder #(.width(4)) adder_2 (.a(bit_extender_3_out), .b(bit_extender_4_out), .out(adder_2_out));  // open: cin, cout
  Adder #(.width(4)) adder_3 (.a(bit_extender_5_out), .b(bit_extender_6_out), .out(adder_3_out));  // open: cin, cout
  Adder #(.width(4)) adder_4 (.a(bit_extender_7_out), .b(bit_extender_8_out), .out(adder_4_out));  // open: cin, cout
  Adder #(.width(4)) adder_5 (.a(adder_1_out), .b(adder_2_out), .out(adder_5_out));  // open: cin, cout
  Adder #(.width(4)) adder_6 (.a(adder_3_out), .b(adder_4_out), .out(adder_6_out));  // open: cin, cout
  Adder #(.width(4)) adder_7 (.a(adder_5_out), .b(adder_6_out), .out(adder_7_out));  // open: cin, cout
  xnor xnor_1 (SUCCESS, CHECK, MINE_IN);
  Multiplexer #(.disabled("Z"), .width(4)) multiplexer_1 (
    .in0(adder_7_out), .in1(4'b1111), .out(multiplexer_1_out), .sel(MINE_IN));
  Multiplexer #(.disabled("Z"), .width(4)) multiplexer_2 (
    .in1(multiplexer_1_out), .out(multiplexer_2_out), .sel(TOUCH));  // open: in0
  Multiplexer #(.disabled("Z"), .width(4)) multiplexer_3 (
    .in0(multiplexer_2_out), .in1(4'b1100), .out(HEXDIGIT), .sel(CHECK));

  assign MINE_OUT = MINE_IN;
endmodule

module PrintSuccess (
  input  SUCCESS,
  output [34:0] OUT1,
  output [34:0] OUT2,
  output [34:0] OUT3,
  output [34:0] OUT4,
  output [34:0] OUT5,
  output [34:0] OUT6,
  output [34:0] OUT7
);

  Multiplexer #(.width(35)) multiplexer_1 (.in0(35'h7f0204081), .in1(35'h7993264cf), .out(OUT1), .sel(SUCCESS));
  Multiplexer #(.width(35)) multiplexer_2 (.in0(35'h7f93264c9), .in1(35'h7f02040ff), .out(OUT2), .sel(SUCCESS));
  Multiplexer #(.width(35)) multiplexer_3 (.in0(35'h4081fe040), .in1(35'h7f83060c1), .out(OUT3), .sel(SUCCESS));
  Multiplexer #(.width(35)) multiplexer_4 (.in0(35'h7993264cf), .in1(35'h7f83060c1), .out(OUT4), .sel(SUCCESS));
  Multiplexer #(.width(35)) multiplexer_5 (.in0(35'h3e83264cf), .in1(35'h7f93264c9), .out(OUT5), .sel(SUCCESS));
  Multiplexer #(.width(35)) multiplexer_6 (.in0(35'h3e83060be), .in1(35'h7993264cf), .out(OUT6), .sel(SUCCESS));
  Multiplexer #(.width(35)) multiplexer_7 (.in0(35'h7d01f407d), .in1(35'h7993264cf), .out(OUT7), .sel(SUCCESS));
  DotMatrix #(.matrixcols(41)) dotmatrix_1 (
    .col0(OUT1[34:28]), .col1(OUT1[27:21]), .col2(OUT1[20:14]), .col3(OUT1[13:7]), .col4(OUT1[6:0]),
    .col5({7{1'b0}}), .col6(OUT2[34:28]), .col7(OUT2[27:21]), .col8(OUT2[20:14]), .col9(OUT2[13:7]),
    .col10(OUT2[6:0]), .col11({7{1'b0}}), .col12(OUT3[34:28]), .col13(OUT3[27:21]), .col14(OUT3[20:14]),
    .col15(OUT3[13:7]), .col16(OUT3[6:0]), .col17({7{1'b0}}), .col18(OUT4[34:28]), .col19(OUT4[27:21]),
    .col20(OUT4[20:14]), .col21(OUT4[13:7]), .col22(OUT4[6:0]), .col23({7{1'b0}}), .col24(OUT5[34:28]),
    .col25(OUT5[27:21]), .col26(OUT5[20:14]), .col27(OUT5[13:7]), .col28(OUT5[6:0]), .col29({7{1'b0}}),
    .col30(OUT6[34:28]), .col31(OUT6[27:21]), .col32(OUT6[20:14]), .col33(OUT6[13:7]), .col34(OUT6[6:0]),
    .col35({7{1'b0}}), .col36(OUT7[34:28]), .col37(OUT7[27:21]), .col38(OUT7[20:14]), .col39(OUT7[13:7]),
    .col40(OUT7[6:0]));
endmodule
